# Fritzing sketch secure-rfid-login-fritzing (saved by Fritzing 0.8.7b)
breadboards: 1

parts:
  J1 = Piezo Speaker
  Componente2 = RFID-RC522
  Componente1 = Arduino Uno (Rev3)

nets:
  GND: J1.pin1, Componente2.GND, Componente1.GND
  N1: J1.pin2, Componente1.D8
  N2: Componente2.SDA, Componente1.D10_PWM/SS
  N3: Componente2.SCK, Componente1.D13/SCK
  N4: Componente2.MOSI, Componente1.D11_PWM/MOSI
  N5: Componente2.MISO, Componente1.D12/MISO
  N6: Componente2.RST, Componente1.D9_PWM
  N7: Componente2.3_3V, Componente1.3V3

custom parts:
  RFID-RC522: The simple China made RFID reader
